// Logisim project processador.circ as structural Verilog: 24 circuits, main circuit Intel 4004
module prototipo__Intel_4004 (
  input  N3,
  input  N2,
  input  N1,
  input  N0,
  input  LOAD_IN
);

  wire clock_1_out, CY_carry_in, memoria_de_dados_1_p3, memoria_de_dados_1_p4, ULA_c_out, undriven_2,
       undriven_7, undriven_8, undriven_10, undriven_11, undriven_12, undriven_13, undriven_14;
  wire [3:0] ACC_p3, adder_2_out, banco_de_registradores_ula_a, banco_de_registradores_ula_b,
       memoria_de_dados_1_p6, multiplexer_1_out, multiplexer_2_out, multiplexer_3_out, multiplexer_4_out,
       multiplexer_5_out, multiplexer_6_out, PC_4, PC_pc, prototipo_entrada_n_1_n, ULA, undriven, undriven_3,
       undriven_4, undriven_5, undriven_6, undriven_9;

  Adder #(.width(4)) adder_1 (.a(PC_pc), .b(4'b0100), .out(PC_4));  // open: cin, cout
  Adder #(.width(4)) adder_2 (.a(PC_pc), .b(undriven), .out(adder_2_out));  // open: cin, cout
  Multiplexer #(.select(2), .width(4)) multiplexer_1 (
    .in1(PC_4), .in2(adder_2_out), .in3(ULA), .out(multiplexer_1_out));  // open: in0, sel, en
  Clock clock_1 (.out(clock_1_out));
  prototipo_PC_Circuit PC (.PC_In(multiplexer_1_out), .Seletor_PC(undriven_2), .clk(clock_1_out), .PC(PC_pc));
  prototipo_Banco_De_Registradores banco_de_registradores (
    .RD(undriven_4), .Resultado(multiplexer_6_out), .clk(clock_1_out), .WriteEn(undriven_7),
    .RG1(undriven_5), .RG2(undriven_6), .ULA_A(banco_de_registradores_ula_a),
    .ULA_B(banco_de_registradores_ula_b));
  // Accumulator ACC: pin names not known; wires that end beside it: ULA, clock_1_out, ACC_p3
  Carry_Register CY (.Carry_ULA(ULA_c_out), .clk(clock_1_out), .Carry_Write(undriven_8), .Carry_In(CY_carry_in));
  Multiplexer #(.width(4)) multiplexer_2 (
    .in0(banco_de_registradores_ula_a), .in1(ACC_p3), .out(multiplexer_2_out));  // open: sel, en
  Multiplexer #(.select(2), .width(4)) multiplexer_3 (
    .in1(banco_de_registradores_ula_b), .in2(undriven_9), .in3(ACC_p3), .out(multiplexer_3_out));  // open: in0, sel, en
  ALU u_ULA (
    .A(multiplexer_2_out), .B(multiplexer_3_out), .C_In(CY_carry_in), .S2(undriven_10), .S1(undriven_11),
    .S0(undriven_12), .SAIDA(ULA), .C_out(ULA_c_out));  // open: OVERFLOW
  Multiplexer #(.width(4)) multiplexer_4 (
    .in0(ULA), .in1(banco_de_registradores_ula_a), .out(multiplexer_4_out), .en(undriven_13));  // open: sel
  Multiplexer #(.width(4)) multiplexer_5 (
    .in0(undriven_3), .in1(banco_de_registradores_ula_b), .out(multiplexer_5_out), .en(undriven_14));  // open: sel
  // Memoria_De_Dados memoria_de_dados_1: pin names not known; wires that end beside it: multiplexer_5_out, multiplexer_4_out, memoria_de_dados_1_p3, memoria_de_dados_1_p4, clock_1_out, memoria_de_dados_1_p6
  prototipo_Entrada_N prototipo_entrada_n_1 (
    .clk(clock_1_out), .N3(N3), .N2(N2), .N1(N1), .N0(N0), .LOAD_IN(LOAD_IN), .N(prototipo_entrada_n_1_n));
  Multiplexer #(.select(2), .width(4)) multiplexer_6 (
    .in0(ULA), .in1(memoria_de_dados_1_p6), .in2(prototipo_entrada_n_1_n), .in3(PC_4), .out(multiplexer_6_out));  // open: sel, en

  // Notes on the sheet:
  //   PC_SELECT
  //   Esse processador tinha muitas mais características do RISC-V
  //   Primeiro protótipo do processador inspirado no Intel 4004
  //   Instrução
  //   Instrução
  //   Imediato
  //   Shifter e extensor
  //   Centro de controle
endmodule

module prototipo_Banco_De_Registradores (
  input  [3:0] RD,
  input  [3:0] Resultado,
  input  clk,
  input  WriteEn,
  input  [3:0] RG1,
  input  [3:0] RG2,
  output [3:0] ULA_A,
  output [3:0] ULA_B
);

  wire decoder_1_out0, decoder_1_out1, decoder_1_out2, decoder_1_out3, decoder_1_out4, decoder_1_out5,
       decoder_1_out6, decoder_1_out7, decoder_1_out8, decoder_1_out9, decoder_1_out10, decoder_1_out11,
       decoder_1_out12, decoder_1_out13, decoder_1_out14, decoder_1_out15;
  wire [3:0] registradores_1_r0, registradores_1_r1, registradores_1_r2, registradores_1_r3,
       registradores_1_r4, registradores_1_r5, registradores_1_r6, registradores_1_r7, registradores_1_r8,
       registradores_1_r9, registradores_1_r10, registradores_1_r11, registradores_1_r12,
       registradores_1_r13, registradores_1_ra_2, registradores_1_sp_2;

  Decoder #(.select(4)) decoder_1 (
    .out0(decoder_1_out0), .out1(decoder_1_out1), .out2(decoder_1_out2), .out3(decoder_1_out3),
    .out4(decoder_1_out4), .out5(decoder_1_out5), .out6(decoder_1_out6), .out7(decoder_1_out7),
    .out8(decoder_1_out8), .out9(decoder_1_out9), .out10(decoder_1_out10), .out11(decoder_1_out11),
    .out12(decoder_1_out12), .out13(decoder_1_out13), .out14(decoder_1_out14), .out15(decoder_1_out15),
    .sel(RD));  // open: en
  Registradores registradores_1 (
    .Load(Resultado), .en0(decoder_1_out0), .en1(decoder_1_out1), .en2(decoder_1_out2), .en3(decoder_1_out3),
    .en4(decoder_1_out4), .en5(decoder_1_out5), .en6(decoder_1_out6), .en7(decoder_1_out7),
    .en8(decoder_1_out8), .en9(decoder_1_out9), .en10(decoder_1_out10), .en11(decoder_1_out11),
    .en12(decoder_1_out12), .en13(decoder_1_out13), .SP(decoder_1_out14), .RA(decoder_1_out15),
    .WriteEnable(WriteEn), .clk(clk), .R0(registradores_1_r0), .R1(registradores_1_r1),
    .R2(registradores_1_r2), .R3(registradores_1_r3), .R4(registradores_1_r4), .R5(registradores_1_r5),
    .R6(registradores_1_r6), .R7(registradores_1_r7), .R8(registradores_1_r8), .R9(registradores_1_r9),
    .R10(registradores_1_r10), .R11(registradores_1_r11), .R12(registradores_1_r12),
    .R13(registradores_1_r13), .SP_2(registradores_1_sp_2), .RA_2(registradores_1_ra_2));
  Multiplexer #(.select(4), .width(4)) multiplexer_1 (
    .in0(registradores_1_r0), .in1(registradores_1_r1), .in2(registradores_1_r2), .in3(registradores_1_r3),
    .in4(registradores_1_r4), .in5(registradores_1_r5), .in6(registradores_1_r6), .in7(registradores_1_r7),
    .in8(registradores_1_r8), .in9(registradores_1_r9), .in10(registradores_1_r10),
    .in11(registradores_1_r11), .in12(registradores_1_r12), .in13(registradores_1_r13),
    .in14(registradores_1_sp_2), .in15(registradores_1_ra_2), .out(ULA_A), .sel(RG1));  // open: en
  Multiplexer #(.select(4), .width(4)) multiplexer_2 (
    .in0(registradores_1_r0), .in1(registradores_1_r1), .in2(registradores_1_r2), .in3(registradores_1_r3),
    .in4(registradores_1_r4), .in5(registradores_1_r5), .in6(registradores_1_r6), .in7(registradores_1_r7),
    .in8(registradores_1_r8), .in9(registradores_1_r9), .in10(registradores_1_r10),
    .in11(registradores_1_r11), .in12(registradores_1_r12), .in13(registradores_1_r13),
    .in14(registradores_1_sp_2), .in15(registradores_1_ra_2), .out(ULA_B), .sel(RG2));  // open: en
endmodule

module Registradores (
  input  [3:0] Load,
  input  en0,
  input  en1,
  input  en2,
  input  en3,
  input  en4,
  input  en5,
  input  en6,
  input  en7,
  input  en8,
  input  en9,
  input  en10,
  input  en11,
  input  en12,
  input  en13,
  input  SP,
  input  RA,
  input  WriteEnable,
  input  clk,
  output [3:0] R0,
  output [3:0] R1,
  output [3:0] R2,
  output [3:0] R3,
  output [3:0] R4,
  output [3:0] R5,
  output [3:0] R6,
  output [3:0] R7,
  output [3:0] R8,
  output [3:0] R9,
  output [3:0] R10,
  output [3:0] R11,
  output [3:0] R12,
  output [3:0] R13,
  output [3:0] SP_2,
  output [3:0] RA_2
);

  wire and_1_out, and_2_out, and_3_out, and_4_out, and_5_out, and_6_out, and_7_out, and_8_out, and_9_out,
       and_10_out, and_11_out, and_12_out, and_13_out, and_14_out, and_15_out, and_16_out;

  and and_1 (and_1_out, en0, WriteEnable);
  and and_2 (and_2_out, en1, WriteEnable);
  and and_3 (and_3_out, en2, WriteEnable);
  and and_4 (and_4_out, en3, WriteEnable);
  and and_5 (and_5_out, en4, WriteEnable);
  and and_6 (and_6_out, en5, WriteEnable);
  and and_7 (and_7_out, en6, WriteEnable);
  and and_8 (and_8_out, en7, WriteEnable);
  and and_9 (and_9_out, en8, WriteEnable);
  and and_10 (and_10_out, en9, WriteEnable);
  and and_11 (and_11_out, en10, WriteEnable);
  and and_12 (and_12_out, en11, WriteEnable);
  and and_13 (and_13_out, en12, WriteEnable);
  and and_14 (and_14_out, en13, WriteEnable);
  and and_15 (and_15_out, SP, WriteEnable);
  and and_16 (and_16_out, RA, WriteEnable);
  Register #(.width(4)) u_R0 (.D(Load), .en(and_1_out), .Q(R0), .clk(clk));  // open: clr
  Register #(.width(4)) u_R1 (.D(Load), .en(and_2_out), .Q(R1), .clk(clk));  // open: clr
  Register #(.width(4)) u_R2 (.D(Load), .en(and_3_out), .Q(R2), .clk(clk));  // open: clr
  Register #(.width(4)) u_R3 (.D(Load), .en(and_4_out), .Q(R3), .clk(clk));  // open: clr
  Register #(.width(4)) u_R4 (.D(Load), .en(and_5_out), .Q(R4), .clk(clk));  // open: clr
  Register #(.width(4)) u_R5 (.D(Load), .en(and_6_out), .Q(R5), .clk(clk));  // open: clr
  Register #(.width(4)) u_R6 (.D(Load), .en(and_7_out), .Q(R6), .clk(clk));  // open: clr
  Register #(.width(4)) u_R7 (.D(Load), .en(and_8_out), .Q(R7), .clk(clk));  // open: clr
  Register #(.width(4)) u_R8 (.D(Load), .en(and_9_out), .Q(R8), .clk(clk));  // open: clr
  Register #(.width(4)) u_R9 (.D(Load), .en(and_10_out), .Q(R9), .clk(clk));  // open: clr
  Register #(.width(4)) u_R10 (.D(Load), .en(and_11_out), .Q(R10), .clk(clk));  // open: clr
  Register #(.width(4)) u_R11 (.D(Load), .en(and_12_out), .Q(R11), .clk(clk));  // open: clr
  Register #(.width(4)) u_R12 (.D(Load), .en(and_13_out), .Q(R12), .clk(clk));  // open: clr
  Register #(.width(4)) u_R13 (.D(Load), .en(and_14_out), .Q(R13), .clk(clk));  // open: clr
  Register #(.width(4)) u_SP (.D(Load), .en(and_15_out), .Q(SP_2), .clk(clk));  // open: clr
  Register #(.width(4)) u_RA (.D(Load), .en(and_16_out), .Q(RA_2), .clk(clk));  // open: clr
endmodule

module ALU (
  input  [3:0] A,
  input  [3:0] B,
  input  C_In,
  input  S2,
  input  S1,
  input  S0,
  output [3:0] SAIDA,
  output C_out,
  output OVERFLOW
);

  wire alu_celula_1bit_1_c_out, alu_celula_1bit_2_c_out, alu_celula_1bit_3_c_out, alu_celula_1bit_4_c_out;
  wire [1:0] not_2_out;

  not not_1 (not_2_out[1], S1);
  not not_2 (not_2_out[0], S0);
  ALU_celula_1bit alu_celula_1bit_1 (
    .A(A[3]), .B(B[3]), .C_in(alu_celula_1bit_2_c_out), .OUT_RESULT(SAIDA[3]), .SEL_OP({S2, not_2_out}),
    .C_out(alu_celula_1bit_1_c_out));
  ALU_overflow alu_overflow_1 (
    .A(A[3]), .B(B[3]), .S(SAIDA[3]), .C_IN(alu_celula_1bit_1_c_out), .SELETOR({S2, not_2_out}),
    .OVERFLOW(OVERFLOW));  // open: OVERFLOW_2
  ALU_celula_1bit alu_celula_1bit_2 (
    .A(A[2]), .B(B[2]), .C_in(alu_celula_1bit_3_c_out), .OUT_RESULT(SAIDA[2]), .SEL_OP({S2, not_2_out}),
    .C_out(alu_celula_1bit_2_c_out));
  ALU_celula_1bit alu_celula_1bit_3 (
    .A(A[1]), .B(B[1]), .C_in(alu_celula_1bit_4_c_out), .OUT_RESULT(SAIDA[1]), .SEL_OP({S2, not_2_out}),
    .C_out(alu_celula_1bit_3_c_out));
  ALU_celula_1bit alu_celula_1bit_4 (
    .A(A[0]), .B(B[0]), .C_in(C_In), .OUT_RESULT(SAIDA[0]), .SEL_OP({S2, not_2_out}),
    .C_out(alu_celula_1bit_4_c_out));
  and AND (C_out, alu_celula_1bit_1_c_out, ~S2);  // AND_Gate

  // Notes on the sheet:
  //   S2    S1   S0
  //   0      0      0        A  +  B  
  //   0      0      1          A  -  B
  //   Tabela de Operaçoes para i 4004
  //   OPERAÇAO
  //   S2    S1   S0
  //   0      0      0        CLEAR  
  //   0      0      1          NAND
  //   0      1      0          A  - B
  //   0      1      1          A + B
  //   1      0      0         A xor B 
  //   1      0      1         A or B
  //   1      1      0        A and B
  //   1      1      1       PRESET
  //   Tabela de Operaçoes Originais da ULA
  //   OPERAÇAO
endmodule

module ALU_celula_1bit (
  input  A,
  input  B,
  input  C_in,
  input  [2:0] SEL_OP,
  output OUT_RESULT,
  output C_out
);

  wire adder_1_cout, adder_1_out, alu_clear_1_out_3, alu_preset_1_out_3, AND_2_out, AND_out, NAND_out,
       OR_out, subtractor_1_bout, subtractor_1_out, XOR_out;

  ALU_clear alu_clear_1 (.in_1(A), .in_2(B), .out_3(alu_clear_1_out_3));
  nand NAND (NAND_out, A, B);
  Adder #(.width(1)) adder_1 (.a(A), .b(B), .out(adder_1_out), .cin(C_in), .cout(adder_1_cout));
  Subtractor #(.width(1)) subtractor_1 (.a(A), .b(B), .out(subtractor_1_out), .bin(C_in), .bout(subtractor_1_bout));
  xor XOR (XOR_out, A, B);
  or OR (OR_out, A, B);
  and AND (AND_out, A, B);
  ALU_preset alu_preset_1 (.in_1(A), .in_2(B), .out_3(alu_preset_1_out_3));
  Multiplexer #(.select(3), .enable("false")) multiplexer_1 (
    .in0(alu_clear_1_out_3), .in1(NAND_out), .in2(adder_1_out), .in3(subtractor_1_out), .in4(XOR_out),
    .in5(OR_out), .in6(AND_out), .in7(alu_preset_1_out_3), .out(OUT_RESULT), .sel(SEL_OP));
  and AND_2 (AND_2_out, ~SEL_OP[2], SEL_OP[1], ~SEL_OP[0]);  // AND_Gate
  Multiplexer #(.enable("false")) multiplexer_2 (
    .in0(adder_1_cout), .in1(subtractor_1_bout), .out(C_out), .sel(AND_2_out));
endmodule

module ALU_preset (
  input  in_1,
  input  in_2,
  output out_3
);


  assign out_3 = 1'b1;
endmodule

module ALU_clear (
  input  in_1,
  input  in_2,
  output out_3
);


  assign out_3 = 1'b0;
endmodule

module ALU_overflow (
  input  A,
  input  B,
  input  S,
  input  C_IN,
  input  [2:0] SELETOR,
  output OVERFLOW,
  output OVERFLOW_2
);

  wire AND_3_out, AND_4_out, AND_out, OR_out, undriven;

  and AND (AND_out, SELETOR[0], SELETOR[1], ~undriven);  // AND_Gate
  and AND_2 (AND_out, SELETOR[0], SELETOR[1], ~undriven);  // AND_Gate
  and AND_3 (AND_3_out, ~A, S, ~B);  // AND_Gate
  and AND_4 (AND_4_out, A, ~S, B);  // AND_Gate
  and AND_5 (AND_4_out, A, ~S, B);  // AND_Gate
  or OR (OR_out, AND_3_out, AND_4_out);
  Multiplexer #(.enable("false")) multiplexer_1 (.in0(OR_out), .in1(C_IN), .out(OVERFLOW), .sel(AND_out));
  Multiplexer #(.enable("false")) multiplexer_2 (.in0(OR_out), .in1(C_IN), .out(OVERFLOW), .sel(AND_out));

  assign OVERFLOW_2 = OVERFLOW;
endmodule

module Memoria_De_Dados (
  input  [3:0] \endereço ,
  input  [7:0] data_in,
  input  Write,
  input  Read,
  input  clock,
  output [7:0] data_out
);

  RAM #(.addrWidth(4), .bus("separate")) ram_1 (
    .addr(\endereço ), .din(data_in), .data(data_out), .str(Write), .clk(clock), .ld(Read));  // open: sel, clr
endmodule

module prototipo_PC_Circuit (
  input  [3:0] PC_In,
  input  Seletor_PC,
  input  clk,
  output [3:0] PC
);

  wire [3:0] adder_1_out, multiplexer_1_out;

  Adder #(.width(4)) adder_1 (.a(PC), .b(4'b0001), .out(adder_1_out));  // open: cin, cout
  Multiplexer #(.width(4)) multiplexer_1 (
    .in0(adder_1_out), .in1(PC_In), .out(multiplexer_1_out), .sel(Seletor_PC));  // open: en
  Register #(.width(4)) u_PC (.D(multiplexer_1_out), .Q(PC), .clk(clk));  // open: en, clr
endmodule

module Accumulator (
  input  [3:0] ACC_In,
  input  ACC_Load,
  input  clk,
  output [3:0] ACC_Out
);

  Register #(.width(4)) register_1 (.D(ACC_In), .en(ACC_Load), .Q(ACC_Out), .clk(clk));  // open: clr
endmodule

module Carry_Register (
  input  Carry_ULA,
  input  clk,
  input  Carry_Write,
  output Carry_In
);

  Register #(.width(1)) register_1 (.D(Carry_ULA), .en(Carry_Write), .Q(Carry_In), .clk(clk));  // open: clr
endmodule

module prototipo_Entrada_N (
  input  clk,
  input  N3,
  input  N2,
  input  N1,
  input  N0,
  input  LOAD_IN,
  output [3:0] N
);

  Register #(.width(4)) register_1 (.D({N3, N2, N1, N0}), .en(LOAD_IN), .Q(N), .clk(clk));  // open: clr

  // Notes on the sheet:
  //   Fazer negócio de guardar clique
endmodule

module Intel_4004 (
  input  Reset,
  input  On,
  input  N3,
  input  N2,
  input  N1,
  input  N0
);

  wire ALU_c_out, clk, CY_carry_in, fib_N, Flag, on_t, timing_and_control_1_acc_write,
       timing_and_control_1_carry_write, \timing_and_control_1_fim_instrução , timing_and_control_1_halt,
       timing_and_control_1_ir_write, timing_and_control_1_memread, timing_and_control_1_memwrite,
       timing_and_control_1_mux_flag_sel, timing_and_control_1_mux_in_de_sel,
       timing_and_control_1_mux_ram_sel, timing_and_control_1_mux_reg_data_sel,
       timing_and_control_1_reg_write;
  wire [2:0] timing_and_control_1_alu_op, timing_and_control_1_mux_acc_sel;
  wire [3:0] ACC_Out, ALU_saida, \banco_de_instruçoes_1_opcode , Banco_de_Registradores_register_out,
       bit_extender_1_out, fib_N_q, Imediato, In_De_crement_reg_new, multiplexer_1_out, multiplexer_3_out, N;
  wire [7:0] Addr, Data_Mem, multiplexer_2_out, PC, undriven;
  wire [24:0] Ctrl;

  Bit_Extender #(.out_width(4)) bit_extender_1 (.in(Data_Mem), .out(bit_extender_1_out));
  Multiplexer #(.select(3), .width(4), .enable("false")) multiplexer_1 (
    .in0(ALU_saida), .in1(bit_extender_1_out), .in2(Imediato), .in3(Banco_de_Registradores_register_out),
    .in4(N), .out(multiplexer_1_out), .sel(timing_and_control_1_mux_acc_sel));  // open: in5, in6, in7
  Accumulator accumulator_1 (
    .ACC_In(multiplexer_1_out), .ACC_Load(timing_and_control_1_acc_write), .clk(clk), .ACC_Out(ACC_Out));
  Flag_flip_flops flag_flip_flops_1 (
    .Select_Flag(timing_and_control_1_mux_flag_sel), .CLK(clk), .Flag(Flag), .Carry_Test(CY_carry_in),
    .Z_test(ACC_Out));
  Carry_Register CY (
    .Carry_ULA(ALU_c_out), .clk(clk), .Carry_Write(timing_and_control_1_carry_write), .Carry_In(CY_carry_in));
  Timing_and_Control timing_and_control_1 (
    .Sinais_de_controle(Ctrl), .Adders(Addr), .Ret(Data_Mem), .Flag(Flag), .hlt(timing_and_control_1_halt),
    .reset(Reset), .CLock(clk), .Carry_Write(timing_and_control_1_carry_write),
    .ALU_OP(timing_and_control_1_alu_op), .MUX_ACC_Sel(timing_and_control_1_mux_acc_sel),
    .ACC_Write(timing_and_control_1_acc_write), .MUX_In_De_sel(timing_and_control_1_mux_in_de_sel),
    .MUX_Reg_Data_Sel(timing_and_control_1_mux_reg_data_sel), .Reg_Write(timing_and_control_1_reg_write),
    .MemWrite(timing_and_control_1_memwrite), .MemRead(timing_and_control_1_memread),
    .IR_Write(timing_and_control_1_ir_write), .\Fim_Instrução (\timing_and_control_1_fim_instrução ),
    .MUX_Flag_Sel(timing_and_control_1_mux_flag_sel), .MUX_RAM_Sel(timing_and_control_1_mux_ram_sel),
    .fib_N__Write(fib_N), .Halt(timing_and_control_1_halt), .PC_Out(PC));
  ALU ALU (
    .A(ACC_Out), .B(Banco_de_Registradores_register_out), .S2(timing_and_control_1_alu_op[2]),
    .S1(timing_and_control_1_alu_op[1]), .S0(timing_and_control_1_alu_op[0]), .SAIDA(ALU_saida),
    .C_out(ALU_c_out));  // open: C_In, OVERFLOW
  \Banco_de_Instruçoes  \banco_de_instruçoes_1  (
    .Opcode(\banco_de_instruçoes_1_opcode ), .Iniciar(on_t), .IR_Write(timing_and_control_1_ir_write),
    .Clk(clk), .Adders(Addr), .Imediato(Imediato), .PC_Out(PC));
  Instruction_Decoder_and_Machine_Cycle_Enconding FSM (
    .Opcode(\banco_de_instruçoes_1_opcode ), .Reset(Reset),
    .\Fim_instrução (\timing_and_control_1_fim_instrução ), .Sinais_de_controle(Ctrl), .Clock(clk));
  Multiplexer #(.width(8), .enable("false")) multiplexer_2 (
    .in0(undriven), .in1(PC), .out(multiplexer_2_out), .sel(timing_and_control_1_mux_ram_sel));
  Memoria_De_Dados Mem_de_Dados (
    .\endereço (Banco_de_Registradores_register_out), .data_in(multiplexer_2_out),
    .Write(timing_and_control_1_memwrite), .Read(timing_and_control_1_memread), .clock(clk),
    .data_out(Data_Mem));
  Multiplexer #(.width(4), .enable("false")) multiplexer_3 (
    .in0(ACC_Out), .in1(In_De_crement_reg_new), .out(multiplexer_3_out),
    .sel(timing_and_control_1_mux_reg_data_sel));
  Entrada_N entrada_n_1 (
    .On(on_t), .N(N), .clk(clk), .Reset(Reset), .Halt(timing_and_control_1_halt), .Ligar(On), .N3(N3),
    .N2(N2), .N1(N1), .N0(N0));
  Bit_Extender #(.out_width(4)) bit_extender_2 (.in(undriven), .out(ACC_Out));
  Banco_de_Registradores Banco_de_Registradores (
    .RD_add(Imediato), .Load_in(multiplexer_3_out), .clk(clk), .RegWrite(timing_and_control_1_reg_write),
    .Read_add(Imediato), .Register_Out(Banco_de_Registradores_register_out));
  In_De_crement_Circuit In_De_crement (
    .Reg(Banco_de_Registradores_register_out), .Select_In_De(timing_and_control_1_mux_in_de_sel),
    .Reg_New(In_De_crement_reg_new));
  LED led_1 (.in(fib_N_q[3]));
  LED led_2 (.in(fib_N_q[1]));
  LED led_3 (.in(fib_N_q[2]));
  Hex_Digit_Display hex_digit_display_1 (.value(fib_N_q));  // open: dp
  Register #(.width(4)) u_fib_N (.D(ACC_Out), .en(fib_N), .Q(fib_N_q), .clk(clk));  // open: clr
  LED led_4 (.in(fib_N_q[0]));

  // Notes on the sheet:
  //   AUTORES:
  //   Processador inspirado no intel 4004, que realiza a operação de fibonacci recursivo
  //   Accumulator
  //   TRABALHO FINAL - PROJETOS DIGITAIS E MICROPROCESSADORES
  //   Arthur Paul Nickel, Bruno Yuuk Hayashi, Luiz Guilherme de Souza Mo e Gabriel Dobrowolski Jorge
  //   Timing and Control
  //   Instruções
  //   Entrada N
  //   UFPR - 2025/2
  //   fib(N) em Hexadecimal e binário
endmodule

module Banco_de_Registradores (
  input  [3:0] RD_add,
  input  [3:0] Load_in,
  input  clk,
  input  RegWrite,
  input  [3:0] Read_add,
  output [3:0] Register_Out
);

  wire decoder_1_out0, decoder_1_out1, decoder_1_out2, decoder_1_out3, decoder_1_out4, decoder_1_out5,
       decoder_1_out6, decoder_1_out7, decoder_1_out8, decoder_1_out9, decoder_1_out10, decoder_1_out11,
       decoder_1_out12, decoder_1_out13, decoder_1_out14, decoder_1_out15;
  wire [3:0] registradores_1_r0, registradores_1_r1, registradores_1_r2, registradores_1_r3,
       registradores_1_r4, registradores_1_r5, registradores_1_r6, registradores_1_r7, registradores_1_r8,
       registradores_1_r9, registradores_1_r10, registradores_1_r11, registradores_1_r12,
       registradores_1_r13, registradores_1_ra_2, registradores_1_sp_2;

  Decoder #(.select(4), .enable("false")) decoder_1 (
    .out0(decoder_1_out0), .out1(decoder_1_out1), .out2(decoder_1_out2), .out3(decoder_1_out3),
    .out4(decoder_1_out4), .out5(decoder_1_out5), .out6(decoder_1_out6), .out7(decoder_1_out7),
    .out8(decoder_1_out8), .out9(decoder_1_out9), .out10(decoder_1_out10), .out11(decoder_1_out11),
    .out12(decoder_1_out12), .out13(decoder_1_out13), .out14(decoder_1_out14), .out15(decoder_1_out15),
    .sel(RD_add));
  Registradores registradores_1 (
    .Load(Load_in), .en0(decoder_1_out0), .en1(decoder_1_out1), .en2(decoder_1_out2), .en3(decoder_1_out3),
    .en4(decoder_1_out4), .en5(decoder_1_out5), .en6(decoder_1_out6), .en7(decoder_1_out7),
    .en8(decoder_1_out8), .en9(decoder_1_out9), .en10(decoder_1_out10), .en11(decoder_1_out11),
    .en12(decoder_1_out12), .en13(decoder_1_out13), .SP(decoder_1_out14), .RA(decoder_1_out15),
    .WriteEnable(RegWrite), .clk(clk), .R0(registradores_1_r0), .R1(registradores_1_r1),
    .R2(registradores_1_r2), .R3(registradores_1_r3), .R4(registradores_1_r4), .R5(registradores_1_r5),
    .R6(registradores_1_r6), .R7(registradores_1_r7), .R8(registradores_1_r8), .R9(registradores_1_r9),
    .R10(registradores_1_r10), .R11(registradores_1_r11), .R12(registradores_1_r12),
    .R13(registradores_1_r13), .SP_2(registradores_1_sp_2), .RA_2(registradores_1_ra_2));
  Multiplexer #(.select(4), .width(4), .enable("false")) multiplexer_1 (
    .in0(registradores_1_r0), .in1(registradores_1_r1), .in2(registradores_1_r2), .in3(registradores_1_r3),
    .in4(registradores_1_r4), .in5(registradores_1_r5), .in6(registradores_1_r6), .in7(registradores_1_r7),
    .in8(registradores_1_r8), .in9(registradores_1_r9), .in10(registradores_1_r10),
    .in11(registradores_1_r11), .in12(registradores_1_r12), .in13(registradores_1_r13),
    .in14(registradores_1_sp_2), .in15(registradores_1_ra_2), .out(Register_Out), .sel(Read_add));
endmodule

module Timing_and_Control (
  input  [24:0] Sinais_de_controle,
  input  [7:0] Adders,
  input  [7:0] Ret,
  input  Flag,
  input  hlt,
  input  reset,
  output CLock,
  output Carry_Write,
  output [2:0] ALU_OP,
  output [2:0] MUX_ACC_Sel,
  output ACC_Write,
  output MUX_In_De_sel,
  output MUX_Reg_Data_Sel,
  output Reg_Write,
  output MemWrite,
  output MemRead,
  output IR_Write,
  output \Fim_Instrução ,
  output MUX_Flag_Sel,
  output MUX_RAM_Sel,
  output fib_N__Write,
  output Halt,
  output [7:0] PC_Out
);

  Clock clock_1 (.out(CLock));
  PC_Circuit PC_Circuit (
    .Addr(Adders), .Ret(Ret), .Seletor_PC(Sinais_de_controle[17:16]), .PC_Write(Sinais_de_controle[18]),
    .Branch(Sinais_de_controle[20]), .Flag(Flag), .clk(CLock), .hlt(hlt), .reset(reset), .PC(PC_Out));

  assign ACC_Write = Sinais_de_controle[7];
  assign ALU_OP = Sinais_de_controle[3:1];
  assign Carry_Write = Sinais_de_controle[0];
  assign fib_N__Write = Sinais_de_controle[23];
  assign \Fim_Instrução  = Sinais_de_controle[19];
  assign Halt = Sinais_de_controle[24];
  assign IR_Write = Sinais_de_controle[15];
  assign MemRead = Sinais_de_controle[14];
  assign MemWrite = Sinais_de_controle[13];
  assign MUX_ACC_Sel = Sinais_de_controle[6:4];
  assign MUX_Flag_Sel = Sinais_de_controle[21];
  assign MUX_In_De_sel = Sinais_de_controle[8];
  assign MUX_RAM_Sel = Sinais_de_controle[22];
  assign MUX_Reg_Data_Sel = Sinais_de_controle[9];
  assign Reg_Write = Sinais_de_controle[10];
  // also tied to GND on the sheet: {Sinais_de_controle[11], Sinais_de_controle[12]}

  // Notes on the sheet:
  //   Distribuição dos sinais de controle,
  //   do clock e implementação do circuito
  //   que define próxima instrução
endmodule

module In_De_crement_Circuit (
  input  [3:0] Reg,
  input  Select_In_De,
  output [3:0] Reg_New
);

  wire [3:0] multiplexer_1_out;

  Multiplexer #(.width(4), .enable("false")) multiplexer_1 (
    .in0(4'b1111), .in1(4'b0001), .out(multiplexer_1_out), .sel(Select_In_De));
  Adder #(.width(4)) adder_1 (.a(Reg), .b(multiplexer_1_out), .out(Reg_New));  // open: cin, cout
endmodule

module Flag_flip_flops (
  input  Select_Flag,
  input  CLK,
  input  Carry_Test,
  input  [3:0] Z_test,
  output Flag
);

  wire and_1_out, Carry_test_q, Z_test_qn;

  and and_1 (and_1_out, Z_test[0], Z_test[1], Z_test[2], Z_test[3]);
  D_Flip_Flop u_Z_test (.clk(CLK), .D(and_1_out), .Qn(Z_test_qn));  // open: Q, preset, en, reset
  D_Flip_Flop u_Carry_test (.clk(CLK), .D(Carry_Test), .Q(Carry_test_q));  // open: Qn, preset, en, reset
  Multiplexer #(.enable("false")) multiplexer_1 (.in0(Z_test_qn), .in1(Carry_test_q), .out(Flag), .sel(Select_Flag));
endmodule

module prototipo_Control (
  input  Clock,
  input  [3:0] Opcode,
  input  Reset,
  output Carry_Write,
  output [2:0] ALU_OP,
  output [2:0] MUX_ACC_Sel,
  output ACC_Write,
  output MUX_In_De_sel,
  output MUX_Reg_Data_Sel,
  output Reg_Write,
  output [1:0] MUX_Addr_Sel,
  output MemWrite,
  output MemRead,
  output IR_Write,
  output [1:0] MUX_Pc_Sel,
  output PC_Write,
  output Branch,
  output MUX_Flag_Sel,
  output MUX_RAM_Sel,
  output fib_N__Write,
  output Halt
);

  wire not_1_out;
  wire [2:0] counter_1_q;
  wire [19:0] rom_1_data;

  Counter #(.width(3), .max('h7)) counter_1 (
    .load(rom_1_data[19]), .D(3'b000), .count(not_1_out), .Q(counter_1_q), .clk(Clock), .clr(Reset));  // open: carry
  not not_1 (not_1_out, rom_1_data[19]);
  ROM #(.addrWidth(7), .dataWidth(25)) rom_1 (
    .addr({Opcode, counter_1_q}),
    .data({Halt, fib_N__Write, MUX_RAM_Sel, MUX_Flag_Sel, Branch, rom_1_data[19], PC_Write, MUX_Pc_Sel, IR_Write, MemRead, MemWrite, MUX_Addr_Sel, Reg_Write, MUX_Reg_Data_Sel, MUX_In_De_sel, ACC_Write, MUX_ACC_Sel, ALU_OP, rom_1_data[0]}));  // open: sel

  // Notes on the sheet:
  //   contents of rom_1 (hex, n*v repeats v):
  //   4c000 800c0 6*0 4c000 800a0 6*0 4c000 800b0 6*0 4c000 80400 6*0 4c000 80081 6*0 4c000 80083 6*0
  //   4c000 400 83000 5*0 4c000 5090 500 80400 4*0 4c000 400 403000 d0000 4*0 4c000 5000 500 e0000 4*0
  //   4c000 44000 d0000 5*0 4c000 44000 1d0000 5*0 4c000 44000 3c0000 5*0 4c000 82800 6*0 4c000 1000000
  //   6*0 4c000 880000
endmodule

module Instruction_Decoder_and_Machine_Cycle_Enconding (
  input  \Fim_instrução ,
  input  [3:0] Opcode,
  input  Clock,
  input  Reset,
  output [24:0] Sinais_de_controle
);

  wire not_1_out;
  wire [2:0] counter_1_q;

  not not_1 (not_1_out, \Fim_instrução );
  Counter #(.width(3), .max('h7)) counter_1 (
    .load(\Fim_instrução ), .D(3'b000), .count(not_1_out), .Q(counter_1_q), .clk(Clock), .clr(Reset));  // open: carry
  ROM #(.addrWidth(7), .dataWidth(25)) rom_1 (.addr({Opcode, counter_1_q}), .data(Sinais_de_controle));  // open: sel

  // Notes on the sheet:
  //   contents of rom_1 (hex, n*v repeats v):
  //   4c000 800c0 6*0 4c000 800a0 6*0 4c000 800b0 6*0 4c000 80400 6*0 4c000 80081 6*0 4c000 80083 6*0
  //   4c000 400 83000 5*0 4c000 5090 500 80400 4*0 4c000 400 403000 d0000 4*0 4c000 5000 500 e0000 4*0
  //   4c000 44000 d0000 5*0 4c000 44000 1d0000 5*0 4c000 44000 3c0000 5*0 4c000 82800 6*0 4c000 1000000
  //   6*0 4c000 880000
endmodule

module PC_Circuit (
  input  [7:0] Addr,
  input  [7:0] Ret,
  input  [1:0] Seletor_PC,
  input  PC_Write,
  input  Branch,
  input  Flag,
  input  clk,
  input  hlt,
  input  reset,
  output [7:0] PC
);

  wire and_1_out, or_1_out, or_2_out;
  wire [7:0] adder_1_out, multiplexer_1_out;

  Adder adder_1 (.a(PC), .b(8'h1), .out(adder_1_out));  // open: cin, cout
  and and_1 (and_1_out, Branch, Flag);
  Multiplexer #(.select(2), .width(8), .enable("false")) multiplexer_1 (
    .in0(adder_1_out), .in1(Addr), .in2(Ret), .out(multiplexer_1_out), .sel(Seletor_PC));  // open: in3
  or or_1 (or_1_out, PC_Write, and_1_out);
  or or_2 (or_2_out, hlt, reset);
  Register u_PC (.D(multiplexer_1_out), .en(or_1_out), .Q(PC), .clk(clk), .clr(or_2_out));

  // Notes on the sheet:
  //   PC_CIRCUIT
endmodule

module \Banco_de_Instruçoes  (
  input  Iniciar,
  input  [7:0] PC_Out,
  input  IR_Write,
  input  Clk,
  output [3:0] Opcode,
  output [7:0] Adders,
  output [3:0] Imediato
);

  wire [7:0] rom_1_data;

  ROM rom_1 (.addr(PC_Out), .data(rom_1_data), .sel(Iniciar));
  Instruction_Register Instruction_Register (
    .Opcode(Opcode), .Instruction(rom_1_data), .IR_Write(IR_Write), .clk(Clk), .Addr(Adders),
    .Imediato(Imediato));

  // Notes on the sheet:
  //   contents of rom_1 (hex, n*v repeats v):
  //   0 b0 2c 8e 8 f0 a0 0 32 2f 6e 22 6e 12 31 22 51 c0 26 11 34 22 54 8e 8 33 7e 32 12 34 22 54 8e 8 43
  //   7e 3f 9e 11 7e 32 7e 3f 9e a0 2c
endmodule

module Instruction_Register (
  input  [7:0] Instruction,
  input  IR_Write,
  input  clk,
  output [7:0] Addr,
  output [3:0] Opcode,
  output [3:0] Imediato
);

  Register register_1 (.D(Instruction), .en(IR_Write), .Q(Addr), .clk(clk));  // open: clr

  assign Imediato = Addr[7:4];
  assign Opcode = Addr[3:0];
endmodule

module Entrada_N (
  input  clk,
  input  Reset,
  input  Halt,
  input  Ligar,
  input  N3,
  input  N2,
  input  N1,
  input  N0,
  output On,
  output [3:0] N
);

  wire and_1_out, and_2_out, or_1_out;

  or or_1 (or_1_out, Reset, and_1_out);
  and and_1 (and_1_out, Halt, ~Ligar);  // AND_Gate
  and and_2 (and_2_out, Ligar, ~Reset);  // AND_Gate
  S_R_Flip_Flop u_On (.S(and_2_out), .clk(clk), .R(or_1_out), .Q(On));  // open: Qn, preset, reset, en

  assign N = {N3, N2, N1, N0};

  // Notes on the sheet:
  //   e pela entrada do número N
  //   Circuito responsável por ligar ou resetar processador ao clicar
endmodule
